// Digital circuit ALU-completa.dig as structural Verilog
module ALU_completa (
  input  [2:0] Seletor,
  input  [7:0] N,
  input  C_AC,
  input  En_AC,
  input  C_MQ,
  input  Q,
  output [7:0] AC,
  output [7:0] MQ
);

  wire _0, decoder_1_out_0, decoder_1_out_1, decoder_1_out_2, decoder_1_out_3, decoder_1_out_4,
       decoder_1_out_5, decoder_1_out_6, En_MQ, not_1_out;
  wire [7:0] circuito_subtracao_1_p3, divisor_8bits_completo_1_p3, divisor_8bits_completo_1_p4, driver_1_out,
       driver_8_out, multiplicador_final_8bits_1_p3, multiplicador_final_8bits_1_p4, nand_1_p3,
       shift_left_1_p2, somador_8bits_1_p3, xor_1_p3;

  Decoder #(.Selector_Bits(3)) decoder_1 (
    .sel(Seletor), .out_0(decoder_1_out_0), .out_1(decoder_1_out_1), .out_2(decoder_1_out_2),
    .out_3(decoder_1_out_3), .out_4(decoder_1_out_4), .out_5(decoder_1_out_5), .out_6(decoder_1_out_6),
    .out_7(_0));
  not not_1 (not_1_out, Seletor[2]);
  and and_1 (En_MQ, Q, Seletor[1], not_1_out);
  // somador_8bits somador_8bits_1: pin names not known; wires that end beside it: AC, N, somador_8bits_1_p3
  // circuito_subtracao circuito_subtracao_1: pin names not known; wires that end beside it: AC, N, circuito_subtracao_1_p3
  // multiplicador_final_8bits multiplicador_final_8bits_1: pin names not known; wires that end beside it: AC, N, multiplicador_final_8bits_1_p3, multiplicador_final_8bits_1_p4
  // divisor_8bits_completo divisor_8bits_completo_1: pin names not known; wires that end beside it: AC, N, divisor_8bits_completo_1_p3, divisor_8bits_completo_1_p4
  // shift_left shift_left_1: pin names not known; wires that end beside it: AC, shift_left_1_p2
  // NAND nand_1: pin names not known; wires that end beside it: AC, N, nand_1_p3
  // XOR xor_1: pin names not known; wires that end beside it: AC, N, xor_1_p3
  assign driver_1_out = decoder_1_out_0 ? somador_8bits_1_p3 : 8'bz;  // Driver driver_1
  assign driver_1_out = decoder_1_out_1 ? circuito_subtracao_1_p3 : 8'bz;  // Driver driver_2
  assign driver_1_out = decoder_1_out_2 ? multiplicador_final_8bits_1_p3 : 8'bz;  // Driver driver_3
  assign driver_1_out = decoder_1_out_3 ? divisor_8bits_completo_1_p4 : 8'bz;  // Driver driver_4
  assign driver_1_out = decoder_1_out_4 ? shift_left_1_p2 : 8'bz;  // Driver driver_5
  assign driver_1_out = decoder_1_out_5 ? nand_1_p3 : 8'bz;  // Driver driver_6
  assign driver_1_out = decoder_1_out_6 ? xor_1_p3 : 8'bz;  // Driver driver_7
  assign driver_8_out = decoder_1_out_2 ? multiplicador_final_8bits_1_p4 : 8'bz;  // Driver driver_8
  assign driver_8_out = decoder_1_out_3 ? divisor_8bits_completo_1_p3 : 8'bz;  // Driver driver_9
  LED led_1 (.in(MQ[6]));
  LED led_2 (.in(MQ[7]));
  Register #(.Bits(8)) register_1 (.D(driver_8_out), .C(C_MQ), .en(En_MQ), .Q(MQ));
  LED led_3 (.in(MQ[4]));
  LED led_4 (.in(MQ[5]));
  LED led_5 (.in(MQ[2]));
  LED led_6 (.in(MQ[3]));
  LED led_7 (.in(MQ[1]));
  LED led_8 (.in(MQ[0]));
  LED led_9 (.in(AC[7]));
  Register #(.Bits(8)) register_2 (.D(driver_1_out), .C(C_AC), .en(En_AC), .Q(AC));
  LED led_10 (.in(AC[5]));
  LED led_11 (.in(AC[6]));
  LED led_12 (.in(AC[3]));
  LED led_13 (.in(AC[4]));
  LED led_14 (.in(AC[2]));
  LED led_15 (.in(AC[1]));
  LED led_16 (.in(AC[0]));

  // Other names for the same wires on the sheet: A[7:0] = AC

  // Notes on the sheet:
  //   MQ
  //   AC
endmodule
