// Digital circuit CPU-8Bits.dig as structural Verilog
module CPU_8Bits (
  input  clk
);

  wire d_ff_1_nq, Q;
  wire [3:0] alu_completa_1_ac, alu_completa_1_ac_2, alu_completa_1_mq, alu_completa_1_mq_2;
  wire [7:0] eeprom_1_d, register_1_q, register_2_q, somador_8bits_1_p3;

  D_FF d_ff_1 (.D(d_ff_1_nq), .C(clk), .Q(Q), .nQ(d_ff_1_nq));
  Register #(.Bits(8)) register_1 (.D(somador_8bits_1_p3), .C(clk), .en(1'b1), .Q(register_1_q));
  // somador_8bits somador_8bits_1: pin names not known; wires that end beside it: register_1_q, 8'h1, somador_8bits_1_p3
  EEPROM #(.AddrBits(8), .Bits(8)) eeprom_1 (.A(register_1_q), .CS(1'b1), .WE(1'b0), .OE(1'b1), .D(eeprom_1_d));
  Register #(.Bits(8)) register_2 (.D(eeprom_1_d), .C(clk), .en(d_ff_1_nq), .Q(register_2_q));
  ALU_completa alu_completa_1 (
    .Seletor(register_2_q[7:5]), .N(eeprom_1_d), .C_AC(clk), .En_AC(Q), .C_MQ(clk), .Q(Q),
    .AC({alu_completa_1_ac_2, alu_completa_1_ac}), .MQ({alu_completa_1_mq_2, alu_completa_1_mq}));
  Seven_Seg_Hex seven_seg_hex_1 (.d(alu_completa_1_mq_2), .dp(1'b0));
  Seven_Seg_Hex seven_seg_hex_2 (.d(alu_completa_1_mq), .dp(1'b0));
  Seven_Seg_Hex seven_seg_hex_3 (.d(alu_completa_1_ac_2), .dp(1'b0));
  Seven_Seg_Hex seven_seg_hex_4 (.d(alu_completa_1_ac), .dp(1'b0));

  // Notes on the sheet:
  //   Unidade de Controle
  //   PC
  //   contents of eeprom_1 (hex, n*v repeats v):
  //   0,5,0,3,20,2
  //   IR
  //   MQ
  //   AC
endmodule
